# Fritzing sketch ATTiny45-Breadboard (saved by Fritzing 0.9.3b)
breadboards: 1

parts:
  2N7000_MOSFET = MOSFET-NCHANNEL [package=to-92]
  U1 = ATTINY13 [package=dip]
  LED1 = LED - 5mm [color="Red (633nm)" package="5 mm [THT]"]
  R1 = Resistor [tolerance=±5% resistance=220 package=THT]
  Cap1 = Ceramic Capacitor [capacitance=0.1µF package="1206 [SMD, multilayer]"]
  R2 = Resistor [tolerance=±5% resistance=220 package=THT]
  LED2 = LED - 5mm [color="Red (633nm)" package="5 mm [THT]"]

nets:
  N1: 2N7000_MOSFET.S, U1.PB5(NRES)
  N2: 2N7000_MOSFET.G, R1.Pin_1, R2.Pin_1
  N3: U1.GND, Cap1.1
  N4: U1.VCC, Cap1.0, LED2.anode
  N5: LED1.cathode, R1.Pin_0
  N6: R2.Pin_0, LED2.cathode
